# Fritzing sketch GPIO0 (saved by Fritzing 0.9.3b)
breadboards: 1

parts:
  B1 = pinbit micro:bit breakout [package="SIP (Single Inline) [THT]"]
  VCC1 = Battery
  S8 = Pushbutton [package=THT]  # not connected
  S9 = Pushbutton [package=THT]

nets:
  N1: B1.pin2, S9.leg1
  N2: B1.GND, S9.leg0
  N3: B1.3v_Power, VCC1.+
  N4: B1.GND_Power, VCC1.-

custom parts:
  pinbit micro:bit breakout: Pmoroni's pin:bit breakout board for micro:bit
  Pushbutton: A generic pushbutton.
