# Fritzing sketch pinbit_microbit_Hello_Real_World_SW (saved by Fritzing 0.9.3b)
breadboards: 1

parts:
  B1 = pinbit micro:bit breakout [package="SIP (Single Inline) [THT]"]
  VCC1 = Battery
  LED1 = LED - 5mm [color="Red (633nm)" package="5 mm [THT]"]
  R1 = Resistor [tolerance=±5% resistance=330 package="0603 [SMD]"]
  S8 = Pushbutton [package=THT]  # not connected
  S9 = Pushbutton [package=THT]

nets:
  N1: B1.pin0, LED1.anode
  N2: B1.pin2, S9.leg1
  N3: B1.GND, R1.Pin_1, S9.leg0
  N4: B1.3v_Power, VCC1.+
  N5: B1.GND_Power, VCC1.-
  N6: LED1.cathode, R1.Pin_0

custom parts:
  pinbit micro:bit breakout: Pmoroni's pin:bit breakout board for micro:bit
  Pushbutton: A generic pushbutton.
