# Fritzing sketch CMMB_GPIO_EXT_example0aE (saved by Fritzing 0.9.3b)
breadboards: 1

parts:
  Q1 = Basic FET N-Channel [package="TO220 [THT]"]
  ギヤードモータ = CHIBI Geared Motor [package="SIP (Single Inline) [THT]"]
  B3 = pinbit micro:bit breakout [package="SIP (Single Inline) [THT]"]
  R2 = Resistor [tolerance=±5% resistance=1k package="0603 [SMD]"]
  R1 = Resistor [tolerance=±5% resistance=10k package="0603 [SMD]"]
  JACK2 = 2.1mm Barrel Jack with Terminal Block

nets:
  N1: Q1.gate, R2.Pin_1, R1.Pin_0
  N2: Q1.drain, ギヤードモータ.pin2
  N3: Q1.source, B3.GND, R1.Pin_1, JACK2.NEG
  N4: ギヤードモータ.pin1, JACK2.POS
  N5: B3.pin0, R2.Pin_0

notes:
  +
  -
  茶黒橙金
  茶黒赤金
  Note: 抵抗値の読み方は０章のリンクを参照
  Note: 消費電力が小さいモーターの場合はmicro:bitの3V端子でも使用可

custom parts:
  CHIBI Geared Motor: Micro Geared Motor
  pinbit micro:bit breakout: Pmoroni's pin:bit breakout board for micro:bit
