# Fritzing sketch pinbit_microbit_motor_sw (saved by Fritzing 0.9.3b)
breadboards: 1

parts:
  VCC2 = Battery
  B4 = pinbit micro:bit breakout [package="SIP (Single Inline) [THT]"]
  ギヤードモータ_1 = CHIBI Geared Motor [package="SIP (Single Inline) [THT]"]
  R3 = Resistor [tolerance=±5% resistance=1k package="0603 [SMD]"]
  R4 = Resistor [tolerance=±5% resistance=10k package="0603 [SMD]"]
  S10 = Pushbutton [package=THT]
  Q2 = Basic FET N-Channel [package="TO220 [THT]"]

nets:
  N1: VCC2.-, B4.GND_Power
  N2: VCC2.+, B4.3v_Power
  N3: B4.pin0, R3.Pin_0
  N4: B4.pin2, S10.leg1
  N5: B4.3v, ギヤードモータ_1.pin1
  N6: B4.GND, R4.Pin_1, S10.leg0, Q2.source
  N7: ギヤードモータ_1.pin2, Q2.drain
  N8: R3.Pin_1, R4.Pin_0, Q2.gate

notes:
  茶黒赤金
  茶黒橙金

custom parts:
  pinbit micro:bit breakout: Pmoroni's pin:bit breakout board for micro:bit
  CHIBI Geared Motor: Micro Geared Motor
  Pushbutton: A generic pushbutton.
