# Fritzing sketch pinbit_gpio_ext1b (saved by Fritzing 0.9.3b)
breadboards: 1

parts:
  B1 = pinbit micro:bit breakout [package="SIP (Single Inline) [THT]"]
  VCC1 = Battery
  VR1 = Trimmer Potentiometer [maximum_resistance=10kΩ package=THT]

nets:
  N1: B1.pin2, VR1.wiper
  N2: B1.3v, VR1.leg1
  N3: B1.GND, VR1.leg2
  N4: B1.3v_Power, VCC1.+
  N5: B1.GND_Power, VCC1.-

custom parts:
  pinbit micro:bit breakout: Pmoroni's pin:bit breakout board for micro:bit
