# Fritzing sketch pinbit_HBridge (saved by Fritzing 0.9.3b)
breadboards: 1

parts:
  ギヤードモータ = CHIBI Geared Motor [package="SIP (Single Inline) [THT]"]
  B3 = pinbit micro:bit breakout [package="SIP (Single Inline) [THT]"]
  VCC1 = Battery
  U1 = L9110 H-bridge module [part_number="L9110 H-bridge"]

nets:
  N1: ギヤードモータ.pin1, U1.MOTOR_A-B
  N2: ギヤードモータ.pin2, U1.MOTOR_A-A
  N3: B3.pin0, U1.A-IB
  N4: B3.pin1, U1.A-IA
  N5: B3.3v, U1.VCC
  GND: B3.GND, U1.GND
  N6: B3.3v_Power, VCC1.+
  N7: B3.GND_Power, VCC1.-

notes:
  Note: 抵抗値の読み方は０章のリンクを参照
  Note: 消費電力が小さいモーターの場合はmicro:bitの3V端子でも使用可
  茶黒赤金
  茶黒橙金
  -
  +

custom parts:
  CHIBI Geared Motor: Micro Geared Motor
  pinbit micro:bit breakout: Pmoroni's pin:bit breakout board for micro:bit
