# Fritzing sketch pinbit_HBridgeE_L298N (saved by Fritzing 0.9.3b)
breadboards: 1

parts:
  ギヤードモータ = CHIBI Geared Motor [package="SIP (Single Inline) [THT]"]
  B3 = pinbit micro:bit breakout [package="SIP (Single Inline) [THT]"]
  VCC1 = Battery
  +5～6V = 2.1mm Barrel Jack with Terminal Block
  L298N1 = L298N DC motor driver

nets:
  N1: ギヤードモータ.pin1, L298N1.OUT4
  N2: ギヤードモータ.pin2, L298N1.OUT3
  N3: B3.pin0, L298N1.IN4
  N4: B3.pin1, L298N1.IN3
  GND: B3.GND, +5～6V.NEG, L298N1.GND
  N5: B3.3v_Power, VCC1.+
  N6: B3.GND_Power, VCC1.-
  N7: +5～6V.POS, L298N1.12V
  N8: L298N1.5V#9, L298N1.ENA
  N9: L298N1.5V#10, L298N1.ENB

notes:
  Note: 抵抗値の読み方は０章のリンクを参照
  Note: 消費電力が小さいモーターの場合はmicro:bitの3V端子でも使用可
  茶黒赤金
  茶黒橙金
  -
  +

custom parts:
  CHIBI Geared Motor: Micro Geared Motor
  pinbit micro:bit breakout: Pmoroni's pin:bit breakout board for micro:bit
  L298N DC motor driver: 2x DC motor driver with 78M05 positive voltage regulator (7..35 V) L298N: max 46 V, 2 A Set 5 V Enable jumper to enable 5 V regultor (needed for the L298N) and +5 V output at screw terminal or supply external +5 V at screw terminal Set ENA and/or ENB to +5 V to enable motor permanently or supply ENA and/or ENB with PWM signal IN1 and IN2 set rotation directory for motor A (OUT1/OUT2) IN2 and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
