# Fritzing sketch pinbit_HBridgeE_MX1508 (saved by Fritzing 0.9.3b)
breadboards: 1

parts:
  ギヤードモータ = CHIBI Geared Motor [package="SIP (Single Inline) [THT]"]
  B3 = pinbit micro:bit breakout [package="SIP (Single Inline) [THT]"]
  VCC1 = Battery
  +5～6V = 2.1mm Barrel Jack with Terminal Block
  MC1 = MX1508 [package="SIP (Single Inline) [THT]"]

nets:
  N1: ギヤードモータ.pin1, MC1.MotorA1
  N2: ギヤードモータ.pin2, MC1.MotorA2
  N3: B3.pin0, MC1.N2
  N4: B3.pin1, MC1.N1
  N5: B3.GND, +5～6V.NEG, MC1.-
  N6: B3.3v_Power, VCC1.+
  N7: B3.GND_Power, VCC1.-
  N8: +5～6V.POS, MC1.+

notes:
  Note: 抵抗値の読み方は０章のリンクを参照
  Note: 消費電力が小さいモーターの場合はmicro:bitの3V端子でも使用可
  茶黒赤金
  茶黒橙金
  -
  +

custom parts:
  CHIBI Geared Motor: Micro Geared Motor
  pinbit micro:bit breakout: Pmoroni's pin:bit breakout board for micro:bit
  MX1508: MX1508 HBridge Motor Controller
