# Fritzing sketch GPIO0b (saved by Fritzing 0.9.3b)
breadboards: 1

parts:
  B1 = pinbit micro:bit breakout [package="SIP (Single Inline) [THT]"]
  VCC1 = Battery
  S8 = Pushbutton [package=THT]  # not connected
  パーツ1 = HC-SR501 Body Sensor Module
  LED1 = smd LED [color="Red (633nm)" package="0603 [SMD]"]
  JACK1 = 2.1mm Barrel Jack with Terminal Block
  R1 = Resistor [tolerance=±5% resistance=680 package="0603 [SMD]"]

nets:
  N1: B1.pin2, パーツ1.OUT, LED1.anode
  GND: B1.GND, パーツ1.GND, JACK1.NEG, R1.Pin_1
  N2: B1.3v_Power, VCC1.+
  N3: B1.GND_Power, VCC1.-
  N4: パーツ1.VCC, JACK1.POS
  N5: LED1.cathode, R1.Pin_0

notes:
  GND
  +5V
  VCC
  OUT

custom parts:
  pinbit micro:bit breakout: Pmoroni's pin:bit breakout board for micro:bit
  Pushbutton: A generic pushbutton.
  HC-SR501 Body Sensor Module: Pyroelectric Infrared PIR Motion Sensor Detector Module
