# Fritzing sketch pinbit_adt7410 (saved by Fritzing 0.9.3b)
breadboards: 1

parts:
  B1 = pinbit micro:bit breakout [package="SIP (Single Inline) [THT]"]
  VCC1 = Battery
  part = ADT7410 AKIZUKI [part_number=ADT7410 package="SIP (Single Inline) [THT]"]

nets:
  N1: B1.pin19, part.pin3
  N2: B1.pin20, part.pin2
  N3: B1.3v, part.pin4
  N4: B1.GND, part.pin1
  N5: B1.3v_Power, VCC1.+
  N6: B1.GND_Power, VCC1.-

custom parts:
  pinbit micro:bit breakout: Pmoroni's pin:bit breakout board for micro:bit
  ADT7410 AKIZUKI: ADT7410 I2C breakout AKIZUKI ver
