# Fritzing sketch CMMB_I2C_example5 (saved by Fritzing 0.9.3b)
breadboards: 1

parts:
  NEOPIXEL2 = Neopixel 8x8 Matrix
  BRD1 = Neopixel I2C
  JACK1 = 2.1mm Barrel Jack with Terminal Block
  B2 = pinbit micro:bit breakout [package="SIP (Single Inline) [THT]"]
  VCC2 = Battery

nets:
  N1: NEOPIXEL2.DIN, BRD1.DATA
  N2: NEOPIXEL2.VCC, BRD1.+5V#6
  N3: NEOPIXEL2.GND, BRD1.GND#8
  N4: BRD1.+3.3V, B2.3v
  N5: BRD1.SDA, B2.pin20
  N6: BRD1.SCL, B2.pin19
  N7: BRD1.GND#3, B2.GND
  N8: BRD1.+5V#4, JACK1.POS
  N9: BRD1.GND#5, JACK1.NEG
  N10: B2.3v_Power, VCC2.+
  N11: B2.GND_Power, VCC2.-

notes:
  5V
  GND
  SDA
  SCL
  DC5V

custom parts:
  Neopixel 8x8 Matrix: Adafruit Neopixel 8x8 Matrix
  Neopixel I2C: neopixel i2c driver board
  pinbit micro:bit breakout: Pmoroni's pin:bit breakout board for micro:bit
