# Fritzing sketch pinbit_bme280 (saved by Fritzing 0.9.3b)
breadboards: 1

parts:
  B1 = pinbit micro:bit breakout [package="SIP (Single Inline) [THT]"]
  VCC1 = Battery
  パーツ3 = BME280 Breakout  # not connected

nets:
  N1: B1.3v_Power, VCC1.+
  N2: B1.GND_Power, VCC1.-

custom parts:
  pinbit micro:bit breakout: Pmoroni's pin:bit breakout board for micro:bit
