# Fritzing sketch pinbit_sht30 (saved by Fritzing 0.9.3b)
breadboards: 1

parts:
  B1 = pinbit micro:bit breakout [package="SIP (Single Inline) [THT]"]
  VCC1 = Battery
  SHT30 = SHT30 breakout [package="SIP (Single Inline) [THT]"]

nets:
  N1: B1.pin19, SHT30.pin3
  N2: B1.pin20, SHT30.pin4
  N3: B1.3v, SHT30.pin1
  N4: B1.GND, SHT30.pin2
  N5: B1.3v_Power, VCC1.+
  N6: B1.GND_Power, VCC1.-

custom parts:
  pinbit micro:bit breakout: Pmoroni's pin:bit breakout board for micro:bit
  SHT30 breakout: SHT30 Temperature Humidity sensor
