# Fritzing sketch pinbit_ADS1115 (saved by Fritzing 0.9.3b)
breadboards: 1

parts:
  B1 = pinbit micro:bit breakout [package="SIP (Single Inline) [THT]"]
  VCC1 = Battery
  パーツ2 = Adafruit ADS1115 16Bit I2C ADC [part_number="Adafruit #1085"]
  R1 = TRIMPOT [package=trim_pot_pth]

nets:
  N1: B1.pin19, パーツ2.SCL
  N2: B1.pin20, パーツ2.SDA
  N3: B1.3v, パーツ2.VDD, R1.CCW
  GND: B1.GND, パーツ2.GND, R1.CW
  N4: B1.3v_Power, VCC1.+
  N5: B1.GND_Power, VCC1.-
  N6: パーツ2.AIN0, R1.WIPER

custom parts:
  pinbit micro:bit breakout: Pmoroni's pin:bit breakout board for micro:bit
  Adafruit ADS1115 16Bit I2C ADC: For microcontrollers without an analog-to-digital converter or when you want a higher-precision ADC, the ADS1115 provides 16-bit precision at 860 samples/second over I2C. The chip can be configured as 4 single-ended input channels, or two differential channels. As a nice bonus, it even includes a programmable gain amplifier, up to x16, to help boost up smaller single/differential signals to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
