# Fritzing sketch pinbit_LoadCell (saved by Fritzing 0.9.3b)
breadboards: 1

parts:
  B1 = pinbit micro:bit breakout [package="SIP (Single Inline) [THT]"]
  VCC1 = Battery
  パーツ2 = Adafruit ADS1115 16Bit I2C ADC [part_number="Adafruit #1085"]
  LoadCell1 = Load Cell [chip_label=LoadCell package="SIP (Single Inline) [THT]"]

nets:
  N1: B1.pin19, パーツ2.SCL
  N2: B1.pin20, パーツ2.SDA
  N3: B1.3v, パーツ2.VDD, LoadCell1.pin4
  GND: B1.GND, パーツ2.GND, LoadCell1.pin3
  N4: B1.3v_Power, VCC1.+
  N5: B1.GND_Power, VCC1.-
  N6: パーツ2.AIN1, LoadCell1.pin2
  N7: パーツ2.AIN0, LoadCell1.pin1

custom parts:
  pinbit micro:bit breakout: Pmoroni's pin:bit breakout board for micro:bit
  Adafruit ADS1115 16Bit I2C ADC: For microcontrollers without an analog-to-digital converter or when you want a higher-precision ADC, the ADS1115 provides 16-bit precision at 860 samples/second over I2C. The chip can be configured as 4 single-ended input channels, or two differential channels. As a nice bonus, it even includes a programmable gain amplifier, up to x16, to help boost up smaller single/differential signals to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
  Load Cell: A SIP stand-in part for whatever you want. With 4 pins on a 300 mil single inline package (SIP) footprint.
