# Fritzing sketch pinbit_AMG8833 (saved by Fritzing 0.9.3b)
breadboards: 1

parts:
  B1 = pinbit micro:bit breakout [package="SIP (Single Inline) [THT]"]
  VCC1 = Battery
  パーツ2 = Adafruit AMG8833 8x8 GRID EYE

nets:
  N1: B1.pin19, パーツ2.SCL
  N2: B1.pin20, パーツ2.SDA
  N3: B1.3v, パーツ2.VIN
  GND: B1.GND, パーツ2.GND
  N4: B1.3v_Power, VCC1.+
  N5: B1.GND_Power, VCC1.-

custom parts:
  pinbit micro:bit breakout: Pmoroni's pin:bit breakout board for micro:bit
