# Fritzing sketch pinbit_BH1750 (saved by Fritzing 0.9.3b)
breadboards: 1

parts:
  B1 = pinbit micro:bit breakout [package="SIP (Single Inline) [THT]"]
  VCC1 = Battery
  パーツ4 = BH1750

nets:
  N1: B1.pin19, パーツ4.SCL
  N2: B1.pin20, パーツ4.SDA
  N3: B1.3v, パーツ4.VCC
  GND: B1.GND, パーツ4.GND
  N4: B1.3v_Power, VCC1.+
  N5: B1.GND_Power, VCC1.-

custom parts:
  pinbit micro:bit breakout: Pmoroni's pin:bit breakout board for micro:bit
  BH1750: Light Sensor
