# Fritzing sketch pinbit_BMP180 (saved by Fritzing 0.9.3b)
breadboards: 1

parts:
  B1 = pinbit micro:bit breakout [package="SIP (Single Inline) [THT]"]
  VCC1 = Battery
  パーツ6 = Barometric Pressure Sensor - BMP180 Breakout (GY-68)

nets:
  N1: B1.pin19, パーツ6.SCL
  N2: B1.pin20, パーツ6.SDA
  N3: B1.3v, パーツ6.VCC
  GND: B1.GND, パーツ6.GND
  N4: B1.3v_Power, VCC1.+
  N5: B1.GND_Power, VCC1.-

notes:
  SDA
  SCL
  GND
  VCC

custom parts:
  pinbit micro:bit breakout: Pmoroni's pin:bit breakout board for micro:bit
