# Fritzing sketch pinbit_INA219 (saved by Fritzing 0.9.3b)
breadboards: 1

parts:
  B1 = pinbit micro:bit breakout [package="SIP (Single Inline) [THT]"]
  VCC1 = Battery
  パーツ5 = INA219 High Side DC Current Sensor Breakout [part_number=904]
  M2 = CHIBI Geared Motor [package="SIP (Single Inline) [THT]"]
  VCC2 = Battery

nets:
  N1: B1.pin19, パーツ5.SCL
  N2: B1.pin20, パーツ5.SDA
  N3: B1.3v, パーツ5.VCC
  GND: B1.GND, パーツ5.GND, M2.pin1, VCC2.-
  N4: B1.3v_Power, VCC1.+
  N5: B1.GND_Power, VCC1.-
  N6: パーツ5.VIN-, M2.pin2
  N7: パーツ5.VIN+, VCC2.+

notes:
  Vin+
  Vin-

custom parts:
  pinbit micro:bit breakout: Pmoroni's pin:bit breakout board for micro:bit
  INA219 High Side DC Current Sensor Breakout: This breakout board will solve all your power-monitoring problems. Instead of struggling with two multimeters, you can just use the handy INA219B chip on this breakout to both measure both the high side voltage and DC current draw over I2C with 1% precision. Most current-measuring devices such as our current panel meter are only good for low side measuring. That means that unless you want to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
  CHIBI Geared Motor: Micro Geared Motor
