# Fritzing sketch pinbit_MLX90614 (saved by Fritzing 0.9.3b)
breadboards: 1

parts:
  B1 = pinbit micro:bit breakout [package="SIP (Single Inline) [THT]"]
  VCC1 = Battery
  MLX90614 = MLX90614 [package="SIP (Single Inline) [THT]"]

nets:
  N1: B1.pin19, MLX90614.pin3
  N2: B1.pin20, MLX90614.pin4
  N3: B1.3v, MLX90614.pin1
  N4: B1.GND, MLX90614.pin2
  N5: B1.3v_Power, VCC1.+
  N6: B1.GND_Power, VCC1.-

custom parts:
  pinbit micro:bit breakout: Pmoroni's pin:bit breakout board for micro:bit
  MLX90614: MLX90614 breakout
