# Fritzing sketch pinbit_MPU6050 (saved by Fritzing 0.9.3b)
breadboards: 1

parts:
  B1 = pinbit micro:bit breakout [package="SIP (Single Inline) [THT]"]
  VCC1 = Battery
  GY1 = MPU-6050 Board GY-521 [form="♀ (female)" package=THT]

nets:
  N1: B1.pin19, GY1.pin3
  N2: B1.pin20, GY1.pin4
  N3: B1.3v, GY1.pin1
  N4: B1.GND, GY1.pin2
  N5: B1.3v_Power, VCC1.+
  N6: B1.GND_Power, VCC1.-

custom parts:
  pinbit micro:bit breakout: Pmoroni's pin:bit breakout board for micro:bit
  MPU-6050 Board GY-521: Acelerometro y Giroscopio MPU-6050 Board GY-521
