# Fritzing sketch pinbit_MPU9250 (saved by Fritzing 0.9.3b)
breadboards: 1

parts:
  B1 = pinbit micro:bit breakout [package="SIP (Single Inline) [THT]"]
  VCC1 = Battery
  MPU9250_MPU-2 = SparkFun IMU Breakout - MPU-9250 [part_number=" SEN-13762"]

nets:
  N1: B1.pin19, MPU9250_MPU-2.SCL/SCLK
  N2: B1.pin20, MPU9250_MPU-2.SDA/SDI
  N3: B1.3v, MPU9250_MPU-2.VDD
  GND: B1.GND, MPU9250_MPU-2.GND
  N4: B1.3v_Power, VCC1.+
  N5: B1.GND_Power, VCC1.-

custom parts:
  pinbit micro:bit breakout: Pmoroni's pin:bit breakout board for micro:bit
