# Fritzing sketch pinbit_MULTI (saved by Fritzing 0.9.3b)
breadboards: 1

parts:
  B1 = pinbit micro:bit breakout [package="SIP (Single Inline) [THT]"]
  VCC1 = Battery
  パーツ4 = BH1750
  U1 = SHT30 breakout [package="SIP (Single Inline) [THT]"]

nets:
  N1: B1.pin19, パーツ4.SCL, U1.pin3
  N2: B1.pin20, パーツ4.SDA, U1.pin4
  N3: B1.3v, パーツ4.VCC, U1.pin1
  GND: B1.GND, パーツ4.GND, U1.pin2
  N4: B1.3v_Power, VCC1.+
  N5: B1.GND_Power, VCC1.-

custom parts:
  pinbit micro:bit breakout: Pmoroni's pin:bit breakout board for micro:bit
  BH1750: Light Sensor
  SHT30 breakout: SHT30 Temperature Humidity sensor
