# Fritzing sketch pinbit_veml6070 (saved by Fritzing 0.9.3b)
breadboards: 1

parts:
  B1 = pinbit micro:bit breakout [package="SIP (Single Inline) [THT]"]
  VCC1 = Battery
  part = VEML6070 [part_number=VEML6070]

nets:
  N1: B1.pin19, part.SCL
  N2: B1.pin20, part.SDA
  N3: B1.3v, part.VDD
  GND: B1.GND, part.GND
  N4: B1.3v_Power, VCC1.+
  N5: B1.GND_Power, VCC1.-

custom parts:
  pinbit micro:bit breakout: Pmoroni's pin:bit breakout board for micro:bit
  VEML6070: This little sensor is a great way to add UV light sensing to any microcontroller project. The VEML6070 from Vishay has a true UV A light sensor and an I2C-controlled ADC that will take readings and integrate them for you over ~60ms to 500ms.
