# Fritzing sketch pinbit_VL53L1X (saved by Fritzing 0.9.3b)
breadboards: 1

parts:
  B1 = pinbit micro:bit breakout [package="SIP (Single Inline) [THT]"]
  VCC1 = Battery
  VL53L1X = VL53L1X [package="SIP (Single Inline) [THT]"]

nets:
  N1: B1.pin19, VL53L1X.pin3
  N2: B1.pin20, VL53L1X.pin2
  N3: B1.3v, VL53L1X.pin1
  N4: B1.GND, VL53L1X.pin4
  N5: B1.3v_Power, VCC1.+
  N6: B1.GND_Power, VCC1.-

custom parts:
  pinbit micro:bit breakout: Pmoroni's pin:bit breakout board for micro:bit
  VL53L1X: VL53L1X breakout
