# Fritzing sketch CMMB_I2C_example7 (saved by Fritzing 0.9.3b)

parts:
  R1 = BBC MicroBit
  SHT30 = SHT30 breakout [package="SIP (Single Inline) [THT]"]

nets:
  N1: R1.GND, SHT30.pin2
  N2: R1.P20_(SDA), SHT30.pin4
  N3: R1.P19_(SCL), SHT30.pin3
  N4: R1.3v3, SHT30.pin1

notes:
  SCL
  SDA
  GND
  3V/VDD

custom parts:
  BBC MicroBit: The BBC MICRO:BIT
  SHT30 breakout: SHT30 Temperature Humidity sensor
