# Fritzing sketch CMMB_I2C_example8 (saved by Fritzing 0.9.3b)

parts:
  R1 = BBC MicroBit
  PCA9685_PWM = PCA9685 16x12-bit PWM Breakout
  MICRO_SERVO = Tower Pro SG90 servo
  MOTOR_Power_5V = 2.1mm Barrel Jack with Terminal Block

nets:
  GND: R1.GND, PCA9685_PWM.no_name_yet#601, PCA9685_PWM.no_name_yet#701, PCA9685_PWM.no_name_yet#1000, MICRO_SERVO.GND, MOTOR_Power_5V.NEG
  N1: R1.P20_(SDA), PCA9685_PWM.no_name_yet#604
  N2: R1.P19_(SCL), PCA9685_PWM.no_name_yet#603
  N3: R1.3v3, PCA9685_PWM.no_name_yet#605
  N4: PCA9685_PWM.no_name_yet#0, MICRO_SERVO.Signal
  N5: PCA9685_PWM.no_name_yet#100, PCA9685_PWM.no_name_yet#706, MICRO_SERVO.+5V, MOTOR_Power_5V.POS

notes:
  SCL
  SDA
  GND
  3V/VDD

custom parts:
  BBC MicroBit: The BBC MICRO:BIT
  Tower Pro SG90 servo: Original file by John De Cristofaro http://www.adafruit.com/products/1449 Adafruit Feedback Servo (Small) Edited by: e-radionica.com 28/9/2015
