# Fritzing sketch pinbit_pca9685 (saved by Fritzing 0.9.3b)
breadboards: 1

parts:
  PCA9685_PWM = PCA9685 16x12-bit PWM Breakout
  MICRO_SERVO = Tower Pro SG90 servo [part_number=101246]
  MOTOR_Power_5V = 2.1mm Barrel Jack with Terminal Block
  B2 = pinbit micro:bit breakout [package="SIP (Single Inline) [THT]"]
  VCC2 = Battery

nets:
  N1: PCA9685_PWM.no_name_yet#0, MICRO_SERVO.Signal
  N2: PCA9685_PWM.no_name_yet#100, PCA9685_PWM.no_name_yet#706, MICRO_SERVO.+5V, MOTOR_Power_5V.POS
  GND: PCA9685_PWM.no_name_yet#601, PCA9685_PWM.no_name_yet#701, PCA9685_PWM.no_name_yet#1000, MICRO_SERVO.GND, MOTOR_Power_5V.NEG, B2.GND
  N3: PCA9685_PWM.no_name_yet#603, B2.pin19
  N4: PCA9685_PWM.no_name_yet#604, B2.pin20
  N5: PCA9685_PWM.no_name_yet#605, B2.3v
  N6: B2.3v_Power, VCC2.+
  N7: B2.GND_Power, VCC2.-

notes:
  SCL
  SDA
  GND
  3V/VDD

custom parts:
  Tower Pro SG90 servo: Original file by John De Cristofaro http://www.adafruit.com/products/1449 Adafruit Feedback Servo (Small) Edited by: e-radionica.com 28/9/2015
  pinbit micro:bit breakout: Pmoroni's pin:bit breakout board for micro:bit
