# Fritzing sketch CMMB_GPIO_EXT_example0 (saved by Fritzing 0.9.3b)
breadboards: 1

parts:
  micro_bit = BBC MicroBit
  LED1 = LED - 5mm [color="Red (633nm)" package="5 mm [THT]"]
  R1 = Resistor [tolerance=±5% resistance=1k part_number="茶黒赤金　　" package="2512 [SMD]"]

nets:
  N1: micro_bit.GND, LED1.cathode
  N2: micro_bit.P1_ANALOG_IN, R1.Pin_0
  N3: LED1.anode, R1.Pin_1

custom parts:
  BBC MicroBit: The BBC MICRO:BIT
