# Fritzing sketch CMMB_GPIO_EXT_example0bE (saved by Fritzing 0.9.3b)

parts:
  パーツ1 = IFR520 MOS module [package=THT]
  B2 = pinbit micro:bit breakout [package="SIP (Single Inline) [THT]"]
  JACK1 = 2.1mm Barrel Jack with Terminal Block
  パーツ2 = IFR520 MOS module [package=THT]
  JACK2 = 2.1mm Barrel Jack with Terminal Block
  ギヤードモータ_1 = CHIBI Geared Motor [package="SIP (Single Inline) [THT]"]
  ギヤードモータ_2 = CHIBI Geared Motor [package="SIP (Single Inline) [THT]"]

nets:
  N1: パーツ1.pin1, B2.pin1
  N2: パーツ1.pin2, パーツ1.pin3, B2.GND
  N3: パーツ1.pin4, ギヤードモータ_1.pin1
  N4: パーツ1.pin5, ギヤードモータ_1.pin2
  N5: パーツ1.pin6, JACK1.POS
  N6: パーツ1.pin7, JACK1.NEG
  N7: パーツ2.pin5, ギヤードモータ_2.pin2
  N8: パーツ2.pin7, JACK2.NEG
  N9: JACK2.POS, ギヤードモータ_2.pin1

notes:
  Note: 抵抗値の読み方は０章のリンクを参照
  茶黒赤金
  茶黒橙金
  -
  +
  モーター電源直結も可
  VCC端子は内部的に使われていません

custom parts:
  pinbit micro:bit breakout: Pmoroni's pin:bit breakout board for micro:bit
  CHIBI Geared Motor: Micro Geared Motor
