# Fritzing sketch CMMB_GPIO_EXT_example1 (saved by Fritzing 0.9.3b)
breadboards: 1

parts:
  micro_bit = BBC MicroBit
  VR = Trimmer Potentiometer [maximum_resistance=10kΩ package=THT]

nets:
  N1: micro_bit.GND, VR.leg2
  N2: micro_bit.3v3, VR.leg1
  N3: micro_bit.P2_-_ANALOG_IN, VR.wiper

custom parts:
  BBC MicroBit: The BBC MICRO:BIT
