# Fritzing sketch CMMB_GPIO_example0 (saved by Fritzing 0.9.3b)
breadboards: 1

parts:
  micro_bit = BBC MicroBit
  S7 = Pushbutton [package=THT]

nets:
  N1: micro_bit.GND, S7.leg1
  N2: micro_bit.P2_-_ANALOG_IN, S7.leg0

custom parts:
  BBC MicroBit: The BBC MICRO:BIT
  Pushbutton: A generic pushbutton.
