# Fritzing sketch CMMB_GPIO_example2 (saved by Fritzing 0.9.3b)
breadboards: 1

parts:
  micro_bit = BBC MicroBit
  S7 = Pushbutton [package=THT]
  LED1 = LED - 5mm [color="Red (633nm)" package="5 mm [THT]"]
  R1 = Resistor [tolerance=±5% resistance=220 package="1206 [SMD]"]

nets:
  N1: micro_bit.GND, S7.leg1, LED1.cathode
  N2: micro_bit.P2_-_ANALOG_IN, S7.leg0
  N3: micro_bit.P0_ANALOG_IN, R1.Pin_0
  N4: LED1.anode, R1.Pin_1

custom parts:
  BBC MicroBit: The BBC MICRO:BIT
  Pushbutton: A generic pushbutton.
