# Fritzing sketch CMMB_GPIO_example3 (saved by Fritzing 0.9.3b)
breadboards: 1

parts:
  micro_bit = BBC MicroBit
  S7 = Pushbutton [package=THT]
  R1 = Resistor [tolerance=±5% resistance=1k part_number="茶黒赤金　　　" package="1206 [SMD]"]
  Q1 = Basic FET N-Channel [package="D2Pak [SMD]"]
  R2 = Resistor [tolerance=±5% resistance=10k part_number="茶黒橙金　　　" package="1206 [SMD]"]
  ギヤードモータ_1 = CHIBI Geared Motor [package="SIP (Single Inline) [THT]"]
  JACK1 = 2.1mm Barrel Jack with Terminal Block [part_number=5V]

nets:
  N1: micro_bit.GND, S7.leg0, Q1.source, R2.Pin_0, JACK1.NEG
  N2: micro_bit.P2_-_ANALOG_IN, S7.leg1
  N3: micro_bit.P0_ANALOG_IN, R1.Pin_1
  N4: R1.Pin_0, Q1.Gate, R2.Pin_1
  N5: Q1.drain, ギヤードモータ_1.pin2
  N6: ギヤードモータ_1.pin1, JACK1.POS

custom parts:
  BBC MicroBit: The BBC MICRO:BIT
  Pushbutton: A generic pushbutton.
  CHIBI Geared Motor: Micro Geared Motor
