# Fritzing sketch CMMB_I2C_example1 (saved by Fritzing 0.9.3b)

parts:
  R1 = BBC MicroBit
  U2 = ADT7410 AKIZUKI [part_number=ADT7410 package="SIP (Single Inline) [THT]"]

nets:
  N1: R1.GND, U2.pin1
  N2: R1.P20_(SDA), U2.pin2
  N3: R1.P19_(SCL), U2.pin3
  N4: R1.3v3, U2.pin4

notes:
  SCL
  SDA
  GND
  3V/VDD

custom parts:
  BBC MicroBit: The BBC MICRO:BIT
  ADT7410 AKIZUKI: ADT7410 I2C breakout AKIZUKI ver
