# Fritzing sketch CMMB_I2C_example2 (saved by Fritzing 0.9.3b)

parts:
  R1 = BBC MicroBit
  パーツ1 = Adafruit_BMP280

nets:
  GND: R1.GND, パーツ1.GND
  N1: R1.P20_(SDA), パーツ1.SDI/SDA
  N2: R1.P19_(SCL), パーツ1.SCK/SCL
  3V3: R1.3v3, パーツ1.3.3V

notes:
  SCL
  SDA
  GND
  3V/VDD

custom parts:
  BBC MicroBit: The BBC MICRO:BIT
  Adafruit_BMP280: Bosch has stepped up their game with their new BMP280 sensor, an environmental sensor with temperature, barometric pressure that is the next generation upgrade to the BMP085/BMP180/BMP183. This sensor is great for all sorts of weather sensing and can even be used in both I2C and SPI! This precision sensor from Bosch is the best low-cost, precision sensing solution for measuring barometric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
