# Fritzing sketch CMMB_I2C_example4 (saved by Fritzing 0.9.3b)

parts:
  R1 = BBC MicroBit
  S11059 = S110569 AKIZUKI [package="SIP (Single Inline) [THT]"]

nets:
  N1: R1.GND, S11059.pin4
  N2: R1.P20_(SDA), S11059.pin2
  N3: R1.P19_(SCL), S11059.pin3
  N4: R1.3v3, S11059.pin1

notes:
  SCL
  SDA
  GND
  3V/VDD

custom parts:
  BBC MicroBit: The BBC MICRO:BIT
  S110569 AKIZUKI: S11059 I2C breakout AKIZUKI ver
