# Fritzing sketch CMMB_I2C_example5 (saved by Fritzing 0.9.3b)

parts:
  NEOPIXEL2 = Neopixel 8x8 Matrix
  BRD1 = Neopixel I2C
  JACK1 = 2.1mm Barrel Jack with Terminal Block
  R6 = BBC MicroBit

nets:
  N1: NEOPIXEL2.DIN, BRD1.DATA
  N2: NEOPIXEL2.VCC, BRD1.+5V#6
  N3: NEOPIXEL2.GND, BRD1.GND#8
  +3.3V: BRD1.+3.3V, R6.3v3
  N4: BRD1.SDA, R6.P20_(SDA)
  N5: BRD1.SCL, R6.P19_(SCL)
  N6: BRD1.GND#3, R6.GND
  N7: BRD1.+5V#4, JACK1.POS
  N8: BRD1.GND#5, JACK1.NEG

notes:
  5V
  GND
  SDA
  SCL

custom parts:
  Neopixel 8x8 Matrix: Adafruit Neopixel 8x8 Matrix
  Neopixel I2C: neopixel i2c driver board
  BBC MicroBit: The BBC MICRO:BIT
