# Fritzing sketch CMMB_I2C_example6 (saved by Fritzing 0.9.3b)

parts:
  R1 = BBC MicroBit
  パーツ2 = BME280 Breakout

nets:
  GND: R1.GND, パーツ2.GND
  N1: R1.P20_(SDA), パーツ2.SDI/SDA
  N2: R1.P19_(SCL), パーツ2.SCK/SCL
  3V3: R1.3v3, パーツ2.3.3V

notes:
  SCL
  SDA
  GND
  3V/VDD

custom parts:
  BBC MicroBit: The BBC MICRO:BIT
