# Fritzing sketch mbit microbit Hello Real World (saved by Fritzing 0.9.3b)
breadboards: 1

parts:
  B1 = m:bit microbit breakout [package="SIP (Single Inline) [THT]"]
  R2 = Resistor [tolerance=±5% resistance=680 package="0603 [SMD]"]
  LED2 = LED - 5mm [color="Red (633nm)" package="5 mm [THT]"]
  VCC2 = Battery

nets:
  N1: B1.pin0, LED2.anode
  N2: B1.GND, R2.Pin_1
  N3: B1.3V_POWER, VCC2.+
  N4: B1.GND_POWER, VCC2.-
  N5: R2.Pin_0, LED2.cathode

custom parts:
  m:bit microbit breakout: m:bit and various generic micro:bit breakout board
