# Fritzing sketch pinbit microbit Hello Real World I2C (saved by Fritzing 0.9.3b)
breadboards: 1

parts:
  B1 = pinbit micro:bit breakout [package="SIP (Single Inline) [THT]"]
  VCC1 = Battery
  S11060 = S110569 AKIZUKI [package="SIP (Single Inline) [THT]"]

nets:
  N1: B1.pin19, S11060.pin3
  N2: B1.pin20, S11060.pin2
  N3: B1.3v, S11060.pin1
  N4: B1.GND, S11060.pin4
  N5: B1.3v_Power, VCC1.+
  N6: B1.GND_Power, VCC1.-

custom parts:
  pinbit micro:bit breakout: Pmoroni's pin:bit breakout board for micro:bit
  S110569 AKIZUKI: S11059 I2C breakout AKIZUKI ver
