# Fritzing sketch test0 (saved by Fritzing 0.9.3b)
breadboards: 1

parts:
  Raspberry_Pi_1 = Raspberry Pi 3 [part_number=RPI-3-V1.2]  # not connected
  R1 = BBC MicroBit
  LED2 = LED - 3mm [color="Red (633nm)" package="3 mm [THT]"]
  R2 = Resistor [tolerance=±5% resistance=1k package="0603 [SMD]"]
  R5 = Trimmer Potentiometer [maximum_resistance=10kΩ package=THT]
  R3 = Resistor [tolerance=±5% resistance=1k package="0603 [SMD]"]
  LED1 = LED - 3mm [color="Red (633nm)" package="3 mm [THT]"]
  パーツ5 = Adafruit VL53L0X Time of Flight Distance Sensor [part_number="Adafruit #3317"]
  NEOPIXEL2 = Neopixel 8x8 Matrix
  BRD1 = Neopixel I2C
  パーツ6 = Adafruit_BMP280
  パーツ7 = Adafruit ADT7410 [part_number="Adafruit #4089"]
  JACK1 = 2.1mm Barrel Jack with Terminal Block

nets:
  GND: R1.GND, LED2.cathode, R5.leg1, LED1.cathode, パーツ5.GND, BRD1.GND#3, BRD1.GND#5, パーツ6.GND, パーツ7.GND, JACK1.NEG
  N1: R1.P20_(SDA), パーツ5.SDA, BRD1.SDA, パーツ6.SDI/SDA, パーツ7.SDA
  N2: R1.P19_(SCL), パーツ5.SCL, BRD1.SCL, パーツ6.SCK/SCL, パーツ7.SCL
  3V3: R1.3v3, R5.leg2, パーツ5.VIN, BRD1.+3.3V, パーツ6.3.3V, パーツ7.VDD
  N3: R1.P2_-_ANALOG_IN, R5.wiper
  N4: R1.P1_ANALOG_IN, R3.Pin_0
  N5: R1.P0_ANALOG_IN, R2.Pin_0
  N6: LED2.anode, R3.Pin_1
  N7: R2.Pin_1, LED1.anode
  N8: NEOPIXEL2.DIN, BRD1.DATA
  N9: NEOPIXEL2.VCC, BRD1.+5V#6
  N10: NEOPIXEL2.GND, BRD1.GND#8
  N11: BRD1.+5V#4, JACK1.POS

notes:
  <-- Wireless connection via BLE -->
  Internal sensors and LEDs
  Triaxial accelerometer, Triaxial magnetometer, Thermometer
  Using web Bluetooth
  Tact switches x2 and matrix LED
  Pin0
  Pin1
  Pin2
  3V
  GND
  5V
  SCL
  SDA

custom parts:
  BBC MicroBit: The BBC MICRO:BIT
  Adafruit VL53L0X Time of Flight Distance Sensor: The VL53L0X is a Time of Flight distance sensor like no other you've used! The sensor contains a very tiny invisible laser source, and a matching sensor. The VL53L0X can detect the "time of flight", or how long the light has taken to bounce back to the sensor. Since it uses a very narrow light source, it is good for determining distance of only the surface directly in front of it. Unlike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
  Neopixel 8x8 Matrix: Adafruit Neopixel 8x8 Matrix
  Neopixel I2C: neopixel i2c driver board
  Adafruit_BMP280: Bosch has stepped up their game with their new BMP280 sensor, an environmental sensor with temperature, barometric pressure that is the next generation upgrade to the BMP085/BMP180/BMP183. This sensor is great for all sorts of weather sensing and can even be used in both I2C and SPI! This precision sensor from Bosch is the best low-cost, precision sensing solution for measuring barometric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
