# Fritzing sketch test1 (saved by Fritzing 0.9.3b)
breadboards: 1

parts:
  R1 = BBC MicroBit
  LED2 = LED - 3mm [color="Red (633nm)" package="3 mm [THT]"]
  R2 = Resistor [tolerance=±5% resistance=1k package="0603 [SMD]"]
  R3 = Resistor [tolerance=±5% resistance=1k package="0603 [SMD]"]
  LED1 = LED - 3mm [color="Red (633nm)" package="3 mm [THT]"]
  パーツ7 = Adafruit ADT7410 [part_number="Adafruit #4089"]

nets:
  GND: R1.GND, LED2.cathode, LED1.cathode, パーツ7.GND
  N1: R1.P20_(SDA), パーツ7.SDA
  N2: R1.P19_(SCL), パーツ7.SCL
  3V3: R1.3v3, パーツ7.VDD
  N3: R1.P1_ANALOG_IN, R3.Pin_0
  N4: R1.P0_ANALOG_IN, R2.Pin_0
  N5: LED2.anode, R3.Pin_1
  N6: R2.Pin_1, LED1.anode

notes:
  Pin0
  Pin1
  3V
  GND
  SCL
  SDA

custom parts:
  BBC MicroBit: The BBC MICRO:BIT
